// Logisim project CPU_CSJ1.circ as structural Verilog: 29 circuits, main circuit main
module main (
  input  in_1,
  input  in_2,
  input  in_3,
  input  in_4
);

  wire and_1_out, and_2_out, and_3_out, and_4_out, and_5_out, and_6_out, and_7_out, and_8_out, and_9_out,
       and_10_out, and_11_out, and_12_out, and_13_out, brance_true_unit_1_jmp, bypassunit_1_bp,
       bypassunit_1_ldes, bypassunit_1_lldes, bypassunit_1_llop0, bypassunit_1_llop1, bypassunit_1_llsrc,
       bypassunit_1_lop0, bypassunit_1_lop1, bypassunit_1_lsrc, bypassunit_1_psw, clock_1_out,
       controlunit_1_hlt, controlunit_1_jmp, not_1_out, or_1_out, or_2_out, or_3_out, ppower_1_cp,
       ppower_1_reset, undriven_2;
  wire [2:0] controlunit_1_alu_op, controlunit_1_beqn3, reg8bit_5_out1, reg8bit_5_out1_2, reg8bit_7_out1_2,
       reg8bit_15_out1_2, reg8bit_23_out1_2;
  wire [3:0] controlunit_1_reg_wd2;
  wire [4:0] reg8bit_7_out1, reg8bit_15_out1, reg8bit_23_out1;
  wire [7:0] alu_1_do, alu_1_psw_e, controlunit_1_mema1, decoder_1to2_1_do, decoder_1to2_2_do,
       decoder_1to2_3_do, decoder_1to2_4_do, decoder_1to2_5_do, decoder_1to2_6_do, decoder_1to2_7_do,
       decoder_1to2_8_do, infinitely_many_reg_1_busa, infinitely_many_reg_1_busb, ram_1_dout, reg8bit_1_out1,
       reg8bit_2_out1, reg8bit_3_out1, reg8bit_4_out1, reg8bit_6_out1, reg8bit_8_out1, reg8bit_9_out1,
       reg8bit_10_out1, reg8bit_11_out1, reg8bit_12_out1, reg8bit_13_out1, reg8bit_14_out1, reg8bit_16_out1,
       reg8bit_17_out1, reg8bit_18_out1, reg8bit_19_out1, reg8bit_20_out1, reg8bit_24_out1, reg8bit_25_out1,
       reg8bit_26_out1, reg8bit_27_out1, reg8bit_28_out1, reg8bit_29_out1, rom_1_data, rom_2_data,
       rom_3_data, selector_4_1_wd, selector_4_2_wd, selector_4_3_wd, selector_4_4_wd, selector_5_1_wd,
       sum8bit_1_out_4, tri_state_gate_1_do, tri_state_gate_2_do, tri_state_gate_5_do, tri_state_gate_6_do;
  wire [7:1] undriven;
  wire [7:6] controlunit_1_brach, reg8bit_5_out1_3;

  Clock clock_1 (.out(clock_1_out));
  ppower ppower_1 (
    .pow(in_1), .res(in_2), .man(in_3), .pul(in_4), .hlt(controlunit_1_hlt), .clk(clock_1_out),
    .cp(ppower_1_cp), .reset(ppower_1_reset));
  decoder_1to2 decoder_1to2_1 (.i1(controlunit_1_jmp), .b(reg8bit_3_out1), .a(sum8bit_1_out_4), .Do(decoder_1to2_1_do));
  sum8bit sum8bit_1 (.a({undriven, 1'b1}), .b(reg8bit_1_out1), .out_4(sum8bit_1_out_4));  // open: ci, co
  reg8bit reg8bit_1 (
    .Di(decoder_1to2_1_do), .clk(ppower_1_cp), .we(ppower_1_cp), .cs(ppower_1_cp), .clr(ppower_1_reset),
    .OUT1(reg8bit_1_out1));  // open: Do
  ROM rom_1 (.addr(reg8bit_1_out1), .data(rom_1_data));
  ROM rom_2 (.addr(reg8bit_1_out1), .data(rom_2_data));
  ROM rom_3 (.addr(reg8bit_1_out1), .data(rom_3_data));
  reg8bit reg8bit_2 (
    .Di(rom_1_data), .clk(ppower_1_cp), .we(ppower_1_cp), .cs(ppower_1_cp), .clr(ppower_1_reset),
    .OUT1(reg8bit_2_out1));  // open: Do
  reg8bit reg8bit_3 (
    .Di(rom_2_data), .clk(ppower_1_cp), .we(ppower_1_cp), .cs(ppower_1_cp), .clr(ppower_1_reset),
    .OUT1(reg8bit_3_out1));  // open: Do
  reg8bit reg8bit_4 (
    .Di(rom_3_data), .clk(ppower_1_cp), .we(ppower_1_cp), .cs(ppower_1_cp), .clr(ppower_1_reset),
    .OUT1(reg8bit_4_out1));  // open: Do
  // Probe on or_3_out
  // Probe on decoder_1to2_7_do
  // Probe on decoder_1to2_8_do
  ControlUnit controlunit_1 (
    .OPcode(reg8bit_2_out1), .ALU_OP(controlunit_1_alu_op), .beqN3(controlunit_1_beqn3),
    .PSW_W(controlunit_1_brach[6]), .Brach(controlunit_1_brach[7]), .MEMA1(controlunit_1_mema1[0]),
    .MEMA0(controlunit_1_mema1[1]), .MEMWD1(controlunit_1_mema1[2]), .MEMWD0(controlunit_1_mema1[3]),
    .MEW(controlunit_1_mema1[4]), .MER(controlunit_1_mema1[5]), .REG_WD2(controlunit_1_reg_wd2[0]),
    .REG_WD1(controlunit_1_reg_wd2[1]), .REG_WD0(controlunit_1_reg_wd2[2]), .REGW(controlunit_1_reg_wd2[3]),
    .jmp(controlunit_1_jmp), .hlt(controlunit_1_hlt));
  infinitely_many_reg infinitely_many_reg_1 (
    .clk(ppower_1_cp), .clr(ppower_1_reset), .we(or_3_out), .Ra(reg8bit_3_out1), .Rb(reg8bit_4_out1),
    .Wa(decoder_1to2_7_do), .W_Data(decoder_1to2_8_do), .BusA(infinitely_many_reg_1_busa),
    .BusB(infinitely_many_reg_1_busb));
  // Probe on infinitely_many_reg_1_busa
  // Probe on infinitely_many_reg_1_busb
  reg8bit reg8bit_5 (
    .Di({controlunit_1_brach, controlunit_1_beqn3, controlunit_1_alu_op}), .clk(ppower_1_cp),
    .we(ppower_1_cp), .cs(ppower_1_cp), .clr(ppower_1_reset),
    .OUT1({reg8bit_5_out1_3, reg8bit_5_out1_2, reg8bit_5_out1}));  // open: Do
  reg8bit reg8bit_6 (
    .Di(controlunit_1_mema1), .clk(ppower_1_cp), .we(ppower_1_cp), .cs(ppower_1_cp), .clr(ppower_1_reset),
    .OUT1(reg8bit_6_out1));  // open: Do
  reg8bit reg8bit_7 (
    .Di({reg8bit_2_out1[2:0], controlunit_1_brach[6], controlunit_1_reg_wd2}), .clk(ppower_1_cp),
    .we(ppower_1_cp), .cs(ppower_1_cp), .clr(ppower_1_reset), .OUT1({reg8bit_7_out1_2, reg8bit_7_out1}));  // open: Do
  reg8bit reg8bit_8 (
    .Di(reg8bit_3_out1), .clk(ppower_1_cp), .we(ppower_1_cp), .cs(ppower_1_cp), .clr(ppower_1_reset),
    .OUT1(reg8bit_8_out1));  // open: Do
  reg8bit reg8bit_9 (
    .Di(reg8bit_4_out1), .clk(ppower_1_cp), .we(ppower_1_cp), .cs(ppower_1_cp), .clr(ppower_1_reset),
    .OUT1(reg8bit_9_out1));  // open: Do
  reg8bit reg8bit_10 (
    .Di(infinitely_many_reg_1_busa), .clk(ppower_1_cp), .we(ppower_1_cp), .cs(ppower_1_cp),
    .clr(ppower_1_reset), .OUT1(reg8bit_10_out1));  // open: Do
  reg8bit reg8bit_11 (
    .Di(infinitely_many_reg_1_busb), .clk(ppower_1_cp), .we(ppower_1_cp), .cs(ppower_1_cp),
    .clr(ppower_1_reset), .OUT1(reg8bit_11_out1));  // open: Do
  Tri_state_Gate tri_state_gate_1 (.Di(selector_4_4_wd), .en(and_1_out), .Do(tri_state_gate_1_do));
  and and_1 (and_1_out, bypassunit_1_psw, bypassunit_1_llsrc);
  BypassUnit bypassunit_1 (
    .ThisSRC(reg8bit_9_out1), .ThisDES(reg8bit_8_out1), .ThisADR(reg8bit_7_out1_2),
    .LastDES(reg8bit_16_out1), .LADR(reg8bit_15_out1_2), .LPSW_W(reg8bit_15_out1[4]),
    .LLastDES(reg8bit_24_out1), .LLADR(reg8bit_23_out1_2), .LLPSW_W(reg8bit_23_out1[4]),
    .PSW_W(reg8bit_7_out1[4]), .LLSRC(bypassunit_1_llsrc), .LSRC(bypassunit_1_lsrc),
    .LLDES(bypassunit_1_lldes), .LDES(bypassunit_1_ldes), .LLOP1(bypassunit_1_llop1),
    .LLOP0(bypassunit_1_llop0), .LOP1(bypassunit_1_lop1), .LOP0(bypassunit_1_lop0), .PSW(bypassunit_1_psw),
    .BP(bypassunit_1_bp));
  Tri_state_Gate tri_state_gate_2 (.Di(selector_4_4_wd), .en(and_2_out), .Do(tri_state_gate_2_do));
  and and_2 (and_2_out, bypassunit_1_psw, bypassunit_1_lldes);
  Tri_state_Gate tri_state_gate_3 (.Di(selector_4_1_wd), .en(and_3_out), .Do(tri_state_gate_1_do));
  Tri_state_Gate tri_state_gate_4 (.Di(selector_4_1_wd), .en(and_6_out), .Do(tri_state_gate_2_do));
  and and_3 (and_3_out, bypassunit_1_lsrc, bypassunit_1_psw);
  and and_4 (and_4_out, or_2_out, reg8bit_5_out1_3[6], bypassunit_1_bp);
  and and_5 (and_5_out, bypassunit_1_bp, reg8bit_5_out1_3[6], or_1_out);
  Tri_state_Gate tri_state_gate_5 (.Di(selector_4_1_wd), .en(and_7_out), .Do(tri_state_gate_5_do));
  and and_6 (and_6_out, bypassunit_1_ldes, bypassunit_1_psw);
  and and_7 (and_7_out, bypassunit_1_lsrc, not_1_out);
  not not_1 (not_1_out, bypassunit_1_psw);
  ALU alu_1 (
    .a1(decoder_1to2_2_do), .b1(decoder_1to2_3_do), .op(reg8bit_5_out1), .Do(alu_1_do),
    .PSW_E(alu_1_psw_e[0]), .PSW_O(alu_1_psw_e[1]), .PSW_Z(alu_1_psw_e[2]), .PSW_P(alu_1_psw_e[3]));
  Tri_state_Gate tri_state_gate_6 (.Di(selector_4_1_wd), .en(and_8_out), .Do(tri_state_gate_6_do));
  and and_8 (and_8_out, bypassunit_1_ldes, not_1_out);
  decoder_1to2 decoder_1to2_2 (.i1(and_4_out), .b(tri_state_gate_2_do), .a(reg8bit_10_out1), .Do(decoder_1to2_2_do));
  decoder_1to2 decoder_1to2_3 (.i1(and_5_out), .b(tri_state_gate_1_do), .a(reg8bit_11_out1), .Do(decoder_1to2_3_do));
  reg8bit reg8bit_12 (
    .Di(alu_1_psw_e), .clk(reg8bit_5_out1_3[6]), .we(reg8bit_5_out1_3[6]), .cs(reg8bit_5_out1_3[6]),
    .clr(ppower_1_reset), .OUT1(reg8bit_12_out1));  // open: Do
  Tri_state_Gate tri_state_gate_7 (.Di(selector_4_4_wd), .en(and_9_out), .Do(tri_state_gate_5_do));
  and and_9 (and_9_out, bypassunit_1_llsrc, not_1_out);
  brance_true_unit brance_true_unit_1 (
    .BEQ_code(reg8bit_5_out1_2), .REG_PSW(reg8bit_12_out1), .jmp(brance_true_unit_1_jmp));
  and and_10 (and_10_out, brance_true_unit_1_jmp, reg8bit_5_out1_3[7]);
  Tri_state_Gate tri_state_gate_8 (.Di(selector_4_4_wd), .en(and_11_out), .Do(tri_state_gate_6_do));
  and and_11 (and_11_out, bypassunit_1_lldes, not_1_out);
  and and_12 (and_12_out, or_1_out, not_1_out, bypassunit_1_bp);
  or or_1 (or_1_out, bypassunit_1_llsrc, bypassunit_1_lsrc);
  decoder_1to2 decoder_1to2_4 (.i1(and_13_out), .b(tri_state_gate_6_do), .a(reg8bit_10_out1), .Do(decoder_1to2_4_do));
  decoder_1to2 decoder_1to2_5 (.i1(and_12_out), .b(tri_state_gate_5_do), .a(reg8bit_11_out1), .Do(decoder_1to2_5_do));
  and and_13 (and_13_out, bypassunit_1_bp, not_1_out, or_2_out);
  or or_2 (or_2_out, bypassunit_1_lldes, bypassunit_1_ldes);
  selector_4 selector_4_1 (
    .a1(bypassunit_1_lop1), .a0(bypassunit_1_lop0), .REG0(reg8bit_19_out1), .REG1(reg8bit_17_out1),
    .REG3(reg8bit_20_out1), .WD(selector_4_1_wd));  // open: REG2
  reg8bit reg8bit_13 (
    .Di({reg8bit_5_out1_3, reg8bit_5_out1_2, reg8bit_5_out1}), .clk(ppower_1_cp), .we(ppower_1_cp),
    .cs(ppower_1_cp), .clr(ppower_1_reset), .OUT1(reg8bit_13_out1));  // open: Do
  reg8bit reg8bit_14 (
    .Di(reg8bit_6_out1), .clk(ppower_1_cp), .we(ppower_1_cp), .cs(ppower_1_cp), .clr(ppower_1_reset),
    .OUT1(reg8bit_14_out1));  // open: Do
  reg8bit reg8bit_15 (
    .Di({reg8bit_7_out1_2, reg8bit_7_out1}), .clk(ppower_1_cp), .we(ppower_1_cp), .cs(ppower_1_cp),
    .clr(ppower_1_reset), .OUT1({reg8bit_15_out1_2, reg8bit_15_out1}));  // open: Do
  reg8bit reg8bit_16 (
    .Di(reg8bit_8_out1), .clk(ppower_1_cp), .we(ppower_1_cp), .cs(ppower_1_cp), .clr(ppower_1_reset),
    .OUT1(reg8bit_16_out1));  // open: Do
  reg8bit reg8bit_17 (
    .Di(reg8bit_9_out1), .clk(ppower_1_cp), .we(ppower_1_cp), .cs(ppower_1_cp), .clr(ppower_1_reset),
    .OUT1(reg8bit_17_out1));  // open: Do
  reg8bit reg8bit_18 (
    .Di(decoder_1to2_5_do), .clk(ppower_1_cp), .we(ppower_1_cp), .cs(ppower_1_cp), .clr(ppower_1_reset),
    .OUT1(reg8bit_18_out1));  // open: Do
  reg8bit reg8bit_19 (
    .Di(decoder_1to2_4_do), .clk(ppower_1_cp), .we(ppower_1_cp), .cs(ppower_1_cp), .clr(ppower_1_reset),
    .OUT1(reg8bit_19_out1));  // open: Do
  reg8bit reg8bit_20 (
    .Di(alu_1_do), .clk(ppower_1_cp), .we(ppower_1_cp), .cs(ppower_1_cp), .clr(ppower_1_reset),
    .OUT1(reg8bit_20_out1));  // open: Do
  selector_4 selector_4_2 (
    .a1(reg8bit_14_out1[0]), .a0(reg8bit_14_out1[1]), .REG0(reg8bit_16_out1), .REG1(reg8bit_17_out1),
    .REG2(reg8bit_18_out1), .REG3(reg8bit_19_out1), .WD(selector_4_2_wd));
  RAM #(.clearpin("true"), .enables("line")) ram_1 (
    .addr(selector_4_2_wd), .we(reg8bit_14_out1[4]), .clk(ppower_1_cp), .din(selector_4_3_wd),
    .dout(ram_1_dout), .clr(undriven_2));
  selector_4 selector_4_3 (
    .a1(reg8bit_14_out1[2]), .a0(reg8bit_14_out1[3]), .REG0(reg8bit_16_out1), .REG1(reg8bit_17_out1),
    .REG2(reg8bit_18_out1), .REG3(reg8bit_19_out1), .WD(selector_4_3_wd));
  decoder_1to2 decoder_1to2_6 (.i1(reg8bit_14_out1[5]), .b(ram_1_dout), .a({8{1'b0}}), .Do(decoder_1to2_6_do));
  selector_4 selector_4_4 (
    .a1(bypassunit_1_llop1), .a0(bypassunit_1_llop0), .REG0(reg8bit_27_out1), .REG1(reg8bit_25_out1),
    .REG2(reg8bit_29_out1), .REG3(reg8bit_28_out1), .WD(selector_4_4_wd));
  reg8bit reg8bit_21 (
    .Di(reg8bit_13_out1), .clk(ppower_1_cp), .we(ppower_1_cp), .cs(ppower_1_cp), .clr(ppower_1_reset));  // open: Do, OUT1
  reg8bit reg8bit_22 (
    .Di(reg8bit_14_out1), .clk(ppower_1_cp), .we(ppower_1_cp), .cs(ppower_1_cp), .clr(ppower_1_reset));  // open: Do, OUT1
  reg8bit reg8bit_23 (
    .Di({reg8bit_15_out1_2, reg8bit_15_out1}), .clk(ppower_1_cp), .we(ppower_1_cp), .cs(ppower_1_cp),
    .clr(ppower_1_reset), .OUT1({reg8bit_23_out1_2, reg8bit_23_out1}));  // open: Do
  reg8bit reg8bit_24 (
    .Di(reg8bit_16_out1), .clk(ppower_1_cp), .we(ppower_1_cp), .cs(ppower_1_cp), .clr(ppower_1_reset),
    .OUT1(reg8bit_24_out1));  // open: Do
  reg8bit reg8bit_25 (
    .Di(reg8bit_17_out1), .clk(ppower_1_cp), .we(ppower_1_cp), .cs(ppower_1_cp), .clr(ppower_1_reset),
    .OUT1(reg8bit_25_out1));  // open: Do
  reg8bit reg8bit_26 (
    .Di(reg8bit_18_out1), .clk(ppower_1_cp), .we(ppower_1_cp), .cs(ppower_1_cp), .clr(ppower_1_reset),
    .OUT1(reg8bit_26_out1));  // open: Do
  reg8bit reg8bit_27 (
    .Di(reg8bit_19_out1), .clk(ppower_1_cp), .we(ppower_1_cp), .cs(ppower_1_cp), .clr(ppower_1_reset),
    .OUT1(reg8bit_27_out1));  // open: Do
  reg8bit reg8bit_28 (
    .Di(reg8bit_20_out1), .clk(ppower_1_cp), .we(ppower_1_cp), .cs(ppower_1_cp), .clr(ppower_1_reset),
    .OUT1(reg8bit_28_out1));  // open: Do
  reg8bit reg8bit_29 (
    .Di(decoder_1to2_6_do), .clk(ppower_1_cp), .we(ppower_1_cp), .cs(ppower_1_cp), .clr(ppower_1_reset),
    .OUT1(reg8bit_29_out1));  // open: Do
  or or_3 (or_3_out, reg8bit_23_out1[3], reg8bit_23_out1[4]);
  decoder_1to2 decoder_1to2_7 (.i1(reg8bit_23_out1[4]), .b(8'h7), .a(reg8bit_24_out1), .Do(decoder_1to2_7_do));
  selector_5 selector_5_1 (
    .a2(reg8bit_23_out1[0]), .a1(reg8bit_23_out1[1]), .a0(reg8bit_23_out1[2]), .REG0(reg8bit_24_out1),
    .REG1(reg8bit_25_out1), .REG2(reg8bit_26_out1), .REG3(reg8bit_27_out1), .REG4(reg8bit_29_out1),
    .WD(selector_5_1_wd));
  decoder_1to2 decoder_1to2_8 (
    .i1(reg8bit_23_out1[4]), .b(reg8bit_28_out1), .a(selector_5_1_wd), .Do(decoder_1to2_8_do));

  // Notes on the sheet:
  //   contents of rom_1 (hex, n*v repeats v):
  //   8 8 10 b
  //   contents of rom_2 (hex, n*v repeats v):
  //   0 1
  //   contents of rom_3 (hex, n*v repeats v):
  //   f f0 1 7
  //   IF/ID
  //   PSW_W信号传入4端口，以代替写psw专属寄存器信号
  //   高三位保存ADR
  //   ID/DX
endmodule

module half_adder (
  input  a,
  input  b,
  output c,
  output s
);

  and and_1 (c, a, b);
  xor xor_1 (s, a, b);
endmodule

module full_adder (
  input  i1,
  input  i2,
  input  ci,
  output co,
  output s
);

  wire half_adder_1_c, half_adder_1_s, half_adder_2_c;

  half_adder half_adder_1 (.a(i1), .b(i2), .c(half_adder_1_c), .s(half_adder_1_s));
  half_adder half_adder_2 (.a(half_adder_1_s), .b(ci), .c(half_adder_2_c), .s(s));
  or or_1 (co, half_adder_1_c, half_adder_2_c);
endmodule

module sum8bit (
  input  [7:0] a,
  input  [7:0] b,
  input  ci,
  output [7:0] out_4,
  output co
);

  wire full_adder_1_co, full_adder_2_co, full_adder_3_co, full_adder_4_co, full_adder_5_co, full_adder_6_co,
       full_adder_7_co;

  full_adder full_adder_1 (.i1(a[0]), .i2(b[0]), .ci(ci), .co(full_adder_1_co), .s(out_4[0]));
  full_adder full_adder_2 (.i1(a[1]), .i2(b[1]), .ci(full_adder_1_co), .co(full_adder_2_co), .s(out_4[1]));
  full_adder full_adder_3 (.i1(a[2]), .i2(b[2]), .ci(full_adder_2_co), .co(full_adder_3_co), .s(out_4[2]));
  full_adder full_adder_4 (.i1(a[3]), .i2(b[3]), .ci(full_adder_3_co), .co(full_adder_4_co), .s(out_4[3]));
  full_adder full_adder_5 (.i1(a[4]), .i2(b[4]), .ci(full_adder_4_co), .co(full_adder_5_co), .s(out_4[4]));
  full_adder full_adder_6 (.i1(a[5]), .i2(b[5]), .ci(full_adder_5_co), .co(full_adder_6_co), .s(out_4[5]));
  full_adder full_adder_7 (.i1(a[6]), .i2(b[6]), .ci(full_adder_6_co), .co(full_adder_7_co), .s(out_4[6]));
  full_adder full_adder_8 (.i1(a[7]), .i2(b[7]), .ci(full_adder_7_co), .co(co), .s(out_4[7]));
endmodule

module reg8bit (
  input  [7:0] Di,
  input  clk,
  input  we,
  input  cs,
  input  clr,
  output [7:0] Do,
  output [7:0] OUT1
);

  wire and_1_out, and_2_out, not_1_out;

  and and_1 (and_1_out, clk, cs, we);
  not not_1 (not_1_out, we);
  Byte byte_1 (.Di(Di), .clk(and_1_out), .clr(clr), .Do(OUT1));
  and and_2 (and_2_out, cs, not_1_out);
  Tri_state_Gate tri_state_gate_1 (.Di(OUT1), .en(and_2_out), .Do(Do));
endmodule

module Byte (
  input  [7:0] Di,
  input  clk,
  input  clr,
  output [7:0] Do
);

  D_Flip_Flop #(.trigger("falling")) d_ff_1 (.clk(clk), .D(Di[0]), .Q(Do[0]), .reset(clr));  // open: Qn, preset
  D_Flip_Flop #(.trigger("falling")) d_ff_2 (.clk(clk), .D(Di[1]), .Q(Do[1]), .reset(clr));  // open: Qn, preset
  D_Flip_Flop #(.trigger("falling")) d_ff_3 (.clk(clk), .D(Di[2]), .Q(Do[2]), .reset(clr));  // open: Qn, preset
  D_Flip_Flop #(.trigger("falling")) d_ff_4 (.clk(clk), .D(Di[3]), .Q(Do[3]), .reset(clr));  // open: Qn, preset
  D_Flip_Flop #(.trigger("falling")) d_ff_5 (.clk(clk), .D(Di[4]), .Q(Do[4]), .reset(clr));  // open: Qn, preset
  D_Flip_Flop #(.trigger("falling")) d_ff_6 (.clk(clk), .D(Di[5]), .Q(Do[5]), .reset(clr));  // open: Qn, preset
  D_Flip_Flop #(.trigger("falling")) d_ff_7 (.clk(clk), .D(Di[6]), .Q(Do[6]), .reset(clr));  // open: Qn, preset
  D_Flip_Flop #(.trigger("falling")) d_ff_8 (.clk(clk), .D(Di[7]), .Q(Do[7]), .reset(clr));  // open: Qn, preset
endmodule

module Tri_state_Gate (
  input  [7:0] Di,
  input  en,
  output [7:0] Do
);

  assign Do = en ? Di : 8'bz;  // Controlled_Buffer controlled_buffer_1
endmodule

module decoder_3to8 (
  input  a2,
  input  a1,
  input  a0,
  output y0,
  output y1,
  output y2,
  output y3,
  output y4,
  output y5,
  output y6,
  output y7
);

  wire not_1_out, not_2_out, not_3_out;

  not not_1 (not_1_out, a2);
  not not_2 (not_2_out, a1);
  not not_3 (not_3_out, a0);
  and and_1 (y7, a0, a1, a2);
  and and_2 (y6, not_3_out, a1, a2);
  and and_3 (y5, a0, not_2_out, a2);
  and and_4 (y4, not_3_out, not_2_out, a2);
  and and_5 (y3, a0, a1, not_1_out);
  and and_6 (y2, not_3_out, a1, not_1_out);
  and and_7 (y1, a0, not_2_out, not_1_out);
  and and_8 (y0, not_1_out, not_2_out, not_3_out);
endmodule

module not8 (
  input  [7:0] Di,
  output [7:0] Do
);

  assign Do = ~Di;  // NOT_Gate not_1, 8 bits wide
endmodule

module ALU (
  input  [7:0] a1,
  input  [7:0] b1,
  input  [2:0] op,
  output [7:0] Do,
  output PSW_E,
  output PSW_O,
  output PSW_Z,
  output PSW_P
);

  wire decoder_3to8_1_y0, decoder_3to8_1_y1, decoder_3to8_1_y2, decoder_3to8_1_y3, decoder_3to8_1_y4,
       decoder_3to8_1_y5, not_1_out, sum8bit_1_co, sum8bit_2_co;
  wire [7:0] and8_1_do, mul_1_do, not8_1_do, not8_2_do, or8_1_do, sum8bit_1_out_4, sum8bit_2_out_4;

  decoder_3to8 decoder_3to8_1 (
    .a2(op[2]), .a1(op[1]), .a0(op[0]), .y0(decoder_3to8_1_y0), .y1(decoder_3to8_1_y1),
    .y2(decoder_3to8_1_y2), .y3(decoder_3to8_1_y3), .y4(decoder_3to8_1_y4), .y5(decoder_3to8_1_y5));  // open: y6, y7
  sum8bit sum8bit_1 (.a(a1), .b(b1), .out_4(sum8bit_1_out_4), .co(sum8bit_1_co));  // open: ci
  Tri_state_Gate tri_state_gate_1 (.Di(sum8bit_1_out_4), .en(decoder_3to8_1_y0), .Do(Do));
  not not_1 (not_1_out, sum8bit_2_co);
  assign PSW_O = decoder_3to8_1_y0 ? sum8bit_1_co : 1'bz;  // Controlled_Buffer controlled_buffer_1
  assign PSW_O = decoder_3to8_1_y1 ? not_1_out : 1'bz;  // Controlled_Buffer controlled_buffer_2
  not8 not8_1 (.Di(b1), .Do(not8_1_do));
  sum8bit sum8bit_2 (.a(a1), .b(not8_1_do), .ci(1'b1), .out_4(sum8bit_2_out_4), .co(sum8bit_2_co));
  Tri_state_Gate tri_state_gate_2 (.Di(sum8bit_2_out_4), .en(decoder_3to8_1_y1), .Do(Do));
  Pull_Resistor pull_resistor_1 (.node(PSW_O));
  MUL mul_1 (.a1(a1[3:0]), .b1(b1[3:0]), .Do(mul_1_do));
  Tri_state_Gate tri_state_gate_3 (.Di(mul_1_do), .en(decoder_3to8_1_y2), .Do(Do));
  not8 not8_2 (.Di(a1), .Do(not8_2_do));
  Tri_state_Gate tri_state_gate_4 (.Di(not8_2_do), .en(decoder_3to8_1_y3), .Do(Do));
  and8 and8_1 (.a1(a1), .b1(b1), .Do(and8_1_do));
  Tri_state_Gate tri_state_gate_5 (.Di(and8_1_do), .en(decoder_3to8_1_y4), .Do(Do));
  or8 or8_1 (.a1(a1), .b1(b1), .Do(or8_1_do));
  Tri_state_Gate tri_state_gate_6 (.Di(or8_1_do), .en(decoder_3to8_1_y5), .Do(Do));
  nor nor_1 (PSW_Z, Do[0], Do[1], Do[2], Do[3], Do[4], Do[5], Do[6], Do[7]);
  not not_2 (PSW_E, Do[0]);
  parity_check parity_check_1 (.I(Do), .O(PSW_P));
endmodule

module and8 (
  input  [7:0] a1,
  input  [7:0] b1,
  output [7:0] Do
);

  assign Do = b1 & a1;  // AND_Gate and_1, 8 bits wide
endmodule

module or8 (
  input  [7:0] a1,
  input  [7:0] b1,
  output [7:0] Do
);

  assign Do = b1 | a1;  // OR_Gate or_1, 8 bits wide
endmodule

module MUL (
  input  [3:0] a1,
  input  [3:0] b1,
  output [7:0] Do
);

  wire full_adder_2_co, full_adder_2_s, full_adder_3_co, full_adder_4_co, full_adder_4_s, full_adder_5_co,
       full_adder_5_s, full_adder_6_co, full_adder_7_co, full_adder_7_s, full_adder_8_co, full_adder_8_s,
       full_adder_9_co, full_adder_9_s, half_adder_1_c, half_adder_2_c, half_adder_3_c;
  wire [3:0] and_1_out, and_2_out, and_3_out;
  wire [3:1] and_4_out;

  full_adder full_adder_1 (.i1(full_adder_3_co), .i2(full_adder_2_co), .ci(and_1_out[3]), .co(Do[7]), .s(Do[6]));
  full_adder full_adder_2 (
    .i1(full_adder_4_co), .i2(and_2_out[3]), .ci(and_1_out[2]), .co(full_adder_2_co), .s(full_adder_2_s));
  assign and_1_out = {4{b1[3]}} & a1;  // AND_Gate and_1, 4 bits wide
  full_adder full_adder_3 (
    .i1(full_adder_6_co), .i2(full_adder_5_co), .ci(full_adder_2_s), .co(full_adder_3_co), .s(Do[5]));
  assign and_2_out = {4{b1[2]}} & a1;  // AND_Gate and_2, 4 bits wide
  full_adder full_adder_4 (.i1(and_2_out[2]), .i2(and_1_out[1]), .ci(1'b0), .co(full_adder_4_co), .s(full_adder_4_s));
  full_adder full_adder_5 (
    .i1(full_adder_7_co), .i2(full_adder_4_s), .ci(and_3_out[3]), .co(full_adder_5_co), .s(full_adder_5_s));
  full_adder full_adder_6 (
    .i1(half_adder_1_c), .i2(full_adder_8_co), .ci(full_adder_5_s), .co(full_adder_6_co), .s(Do[4]));
  full_adder full_adder_7 (
    .i1(and_3_out[2]), .i2(and_2_out[1]), .ci(and_1_out[0]), .co(full_adder_7_co), .s(full_adder_7_s));
  full_adder full_adder_8 (
    .i1(full_adder_9_co), .i2(full_adder_7_s), .ci(and_4_out[3]), .co(full_adder_8_co), .s(full_adder_8_s));
  half_adder half_adder_1 (.a(half_adder_2_c), .b(full_adder_8_s), .c(half_adder_1_c), .s(Do[3]));
  assign and_3_out = {4{b1[1]}} & a1;  // AND_Gate and_3, 4 bits wide
  full_adder full_adder_9 (
    .i1(and_4_out[2]), .i2(and_3_out[1]), .ci(and_2_out[0]), .co(full_adder_9_co), .s(full_adder_9_s));
  half_adder half_adder_2 (.a(half_adder_3_c), .b(full_adder_9_s), .c(half_adder_2_c), .s(Do[2]));
  assign {and_4_out, Do[0]} = {4{b1[0]}} & a1;  // AND_Gate and_4, 4 bits wide
  half_adder half_adder_3 (.a(and_4_out[1]), .b(and_3_out[0]), .c(half_adder_3_c), .s(Do[1]));
endmodule

module ppower (
  input  pow,
  input  res,
  input  man,
  input  pul,
  input  hlt,
  input  clk,
  output cp,
  output reset
);

  wire and_1_out, and_2_out, and_3_out, not_1_out, not_2_out, not_3_out, not_4_out, not_5_out;

  not not_1 (not_1_out, pow);
  not not_2 (not_2_out, res);
  not not_3 (not_3_out, man);
  not not_4 (not_4_out, pul);
  not not_5 (not_5_out, hlt);
  and and_1 (and_1_out, clk, not_2_out, pow, not_3_out, not_5_out);
  and and_2 (and_2_out, not_2_out, pow, man, pul, not_5_out);
  or or_1 (cp, and_1_out, and_2_out);
  and and_3 (and_3_out, pow, res);
  or or_2 (reset, and_3_out, not_1_out);
endmodule

module ccounter (
  input  cp,
  input  clr,
  output [7:0] y
);

  wire t_ff_1_qn, t_ff_2_qn, t_ff_3_qn, t_ff_4_qn, t_ff_5_qn, t_ff_6_qn, t_ff_7_qn;

  T_Flip_Flop t_ff_1 (.clk(cp), .T(1'b1), .Q(y[0]), .Qn(t_ff_1_qn), .reset(clr));  // open: preset
  T_Flip_Flop t_ff_2 (.clk(t_ff_1_qn), .T(t_ff_1_qn), .Q(y[1]), .Qn(t_ff_2_qn), .reset(clr));  // open: preset
  T_Flip_Flop t_ff_3 (.clk(t_ff_2_qn), .T(t_ff_2_qn), .Q(y[2]), .Qn(t_ff_3_qn), .reset(clr));  // open: preset
  T_Flip_Flop t_ff_4 (.clk(t_ff_3_qn), .T(t_ff_3_qn), .Q(y[3]), .Qn(t_ff_4_qn), .reset(clr));  // open: preset
  T_Flip_Flop t_ff_5 (.clk(t_ff_4_qn), .T(t_ff_4_qn), .Q(y[4]), .Qn(t_ff_5_qn), .reset(clr));  // open: preset
  T_Flip_Flop t_ff_6 (.clk(t_ff_5_qn), .T(t_ff_5_qn), .Q(y[5]), .Qn(t_ff_6_qn), .reset(clr));  // open: preset
  T_Flip_Flop t_ff_7 (.clk(t_ff_6_qn), .T(t_ff_6_qn), .Q(y[6]), .Qn(t_ff_7_qn), .reset(clr));  // open: preset
  T_Flip_Flop t_ff_8 (.clk(t_ff_7_qn), .T(t_ff_7_qn), .Q(y[7]), .reset(clr));  // open: Qn, preset
endmodule

module decoder_1to2 (
  input  i1,
  input  [7:0] b,
  input  [7:0] a,
  output [7:0] Do
);

  wire not_1_out;

  not not_1 (not_1_out, i1);
  Tri_state_Gate tri_state_gate_1 (.Di(a), .en(not_1_out), .Do(Do));
  Tri_state_Gate tri_state_gate_2 (.Di(b), .en(i1), .Do(Do));
endmodule

module decoder_5to32 (
  input  a0,
  input  a1,
  input  a2,
  input  a3,
  input  a4,
  output [31:0] uo
);

  wire decoder_2to4_1_y0, decoder_2to4_1_y1, decoder_2to4_1_y2, decoder_2to4_1_y3;
  wire [7:0] decoder_3to8_1_y0, decoder_3to8_2_y0, decoder_3to8_3_y0, decoder_3to8_4_y0;

  decoder_3to8 decoder_3to8_1 (
    .a2(a2), .a1(a1), .a0(a0), .y0(decoder_3to8_1_y0[0]), .y1(decoder_3to8_1_y0[1]),
    .y2(decoder_3to8_1_y0[2]), .y3(decoder_3to8_1_y0[3]), .y4(decoder_3to8_1_y0[4]),
    .y5(decoder_3to8_1_y0[5]), .y6(decoder_3to8_1_y0[6]), .y7(decoder_3to8_1_y0[7]));
  decoder_3to8 decoder_3to8_2 (
    .a2(a2), .a1(a1), .a0(a0), .y0(decoder_3to8_2_y0[0]), .y1(decoder_3to8_2_y0[1]),
    .y2(decoder_3to8_2_y0[2]), .y3(decoder_3to8_2_y0[3]), .y4(decoder_3to8_2_y0[4]),
    .y5(decoder_3to8_2_y0[5]), .y6(decoder_3to8_2_y0[6]), .y7(decoder_3to8_2_y0[7]));
  decoder_3to8 decoder_3to8_3 (
    .a2(a2), .a1(a1), .a0(a0), .y0(decoder_3to8_3_y0[0]), .y1(decoder_3to8_3_y0[1]),
    .y2(decoder_3to8_3_y0[2]), .y3(decoder_3to8_3_y0[3]), .y4(decoder_3to8_3_y0[4]),
    .y5(decoder_3to8_3_y0[5]), .y6(decoder_3to8_3_y0[6]), .y7(decoder_3to8_3_y0[7]));
  decoder_3to8 decoder_3to8_4 (
    .a2(a2), .a1(a1), .a0(a0), .y0(decoder_3to8_4_y0[0]), .y1(decoder_3to8_4_y0[1]),
    .y2(decoder_3to8_4_y0[2]), .y3(decoder_3to8_4_y0[3]), .y4(decoder_3to8_4_y0[4]),
    .y5(decoder_3to8_4_y0[5]), .y6(decoder_3to8_4_y0[6]), .y7(decoder_3to8_4_y0[7]));
  decoder_2to4 decoder_2to4_1 (
    .a1(a4), .a0(a3), .y0(decoder_2to4_1_y0), .y1(decoder_2to4_1_y1), .y2(decoder_2to4_1_y2),
    .y3(decoder_2to4_1_y3));
  Tri_state_Gate tri_state_gate_1 (.Di(decoder_3to8_1_y0), .en(decoder_2to4_1_y0), .Do(uo[7:0]));
  Tri_state_Gate tri_state_gate_2 (.Di(decoder_3to8_2_y0), .en(decoder_2to4_1_y1), .Do(uo[15:8]));
  Tri_state_Gate tri_state_gate_3 (.Di(decoder_3to8_3_y0), .en(decoder_2to4_1_y2), .Do(uo[23:16]));
  Tri_state_Gate tri_state_gate_4 (.Di(decoder_3to8_4_y0), .en(decoder_2to4_1_y3), .Do(uo[31:24]));
  Pull_Resistor pull_resistor_1 (.node(uo));
endmodule

module decoder_2to4 (
  input  a1,
  input  a0,
  output y0,
  output y1,
  output y2,
  output y3
);

  decoder_3to8 decoder_3to8_1 (.a1(a1), .a0(a0), .y0(y0), .y1(y1), .y2(y2), .y3(y3));  // open: a2, y4, y5, y6, y7
endmodule

module infinitely_many_reg (
  input  clk,
  input  clr,
  input  we,
  input  [7:0] Ra,
  input  [7:0] Rb,
  input  [7:0] Wa,
  input  [7:0] W_Data,
  output [7:0] BusA,
  output [7:0] BusB
);

  wire [7:0] reg8bit_1_out1, reg8bit_2_out1, reg8bit_3_out1, reg8bit_4_out1, reg8bit_5_out1, reg8bit_6_out1,
       reg8bit_7_out1, reg8bit_8_out1;
  wire [31:0] decoder_5to32_1_uo, decoder_5to32_2_uo, decoder_5to32_3_uo;

  decoder_5to32 decoder_5to32_1 (.a0(Wa[0]), .a1(Wa[1]), .a2(Wa[2]), .a3(Wa[3]), .a4(Wa[4]), .uo(decoder_5to32_1_uo));
  decoder_5to32 decoder_5to32_2 (.a0(Ra[0]), .a1(Ra[1]), .a2(Ra[2]), .a3(Ra[3]), .a4(Ra[4]), .uo(decoder_5to32_2_uo));
  decoder_5to32 decoder_5to32_3 (.a0(Rb[0]), .a1(Rb[1]), .a2(Rb[2]), .a3(Rb[3]), .a4(Rb[4]), .uo(decoder_5to32_3_uo));
  reg8bit reg8bit_1 (
    .Di(W_Data), .clk(clk), .we(we), .cs(decoder_5to32_1_uo[0]), .clr(clr), .OUT1(reg8bit_1_out1));  // open: Do
  reg8bit reg8bit_2 (
    .Di(W_Data), .clk(clk), .we(we), .cs(decoder_5to32_1_uo[1]), .clr(clr), .OUT1(reg8bit_2_out1));  // open: Do
  reg8bit reg8bit_3 (
    .Di(W_Data), .clk(clk), .we(we), .cs(decoder_5to32_1_uo[2]), .clr(clr), .OUT1(reg8bit_3_out1));  // open: Do
  reg8bit reg8bit_4 (
    .Di(W_Data), .clk(clk), .we(we), .cs(decoder_5to32_1_uo[3]), .clr(clr), .OUT1(reg8bit_4_out1));  // open: Do
  reg8bit reg8bit_5 (
    .Di(W_Data), .clk(clk), .we(we), .cs(decoder_5to32_1_uo[4]), .clr(clr), .OUT1(reg8bit_5_out1));  // open: Do
  reg8bit reg8bit_6 (
    .Di(W_Data), .clk(clk), .we(we), .cs(decoder_5to32_1_uo[5]), .clr(clr), .OUT1(reg8bit_6_out1));  // open: Do
  reg8bit reg8bit_7 (
    .Di(W_Data), .clk(clk), .we(we), .cs(decoder_5to32_1_uo[6]), .clr(clr), .OUT1(reg8bit_7_out1));  // open: Do
  reg8bit reg8bit_8 (
    .Di(W_Data), .clk(clk), .we(we), .cs(decoder_5to32_1_uo[7]), .clr(clr), .OUT1(reg8bit_8_out1));  // open: Do
  Tri_state_Gate tri_state_gate_1 (.Di(reg8bit_1_out1), .en(decoder_5to32_2_uo[0]), .Do(BusA));
  Tri_state_Gate tri_state_gate_2 (.Di(reg8bit_1_out1), .en(decoder_5to32_3_uo[0]), .Do(BusB));
  Tri_state_Gate tri_state_gate_3 (.Di(reg8bit_2_out1), .en(decoder_5to32_2_uo[1]), .Do(BusA));
  Tri_state_Gate tri_state_gate_4 (.Di(reg8bit_2_out1), .en(decoder_5to32_3_uo[1]), .Do(BusB));
  Tri_state_Gate tri_state_gate_5 (.Di(reg8bit_3_out1), .en(decoder_5to32_2_uo[2]), .Do(BusA));
  Tri_state_Gate tri_state_gate_6 (.Di(reg8bit_3_out1), .en(decoder_5to32_3_uo[2]), .Do(BusB));
  Tri_state_Gate tri_state_gate_7 (.Di(reg8bit_4_out1), .en(decoder_5to32_2_uo[3]), .Do(BusA));
  Tri_state_Gate tri_state_gate_8 (.Di(reg8bit_4_out1), .en(decoder_5to32_3_uo[3]), .Do(BusB));
  Tri_state_Gate tri_state_gate_9 (.Di(reg8bit_5_out1), .en(decoder_5to32_2_uo[4]), .Do(BusA));
  Tri_state_Gate tri_state_gate_10 (.Di(reg8bit_5_out1), .en(decoder_5to32_3_uo[4]), .Do(BusB));
  Tri_state_Gate tri_state_gate_11 (.Di(reg8bit_6_out1), .en(decoder_5to32_2_uo[5]), .Do(BusA));
  Tri_state_Gate tri_state_gate_12 (.Di(reg8bit_6_out1), .en(decoder_5to32_3_uo[5]), .Do(BusB));
  Tri_state_Gate tri_state_gate_13 (.Di(reg8bit_7_out1), .en(decoder_5to32_2_uo[6]), .Do(BusA));
  Tri_state_Gate tri_state_gate_14 (.Di(reg8bit_7_out1), .en(decoder_5to32_3_uo[6]), .Do(BusB));
  Tri_state_Gate tri_state_gate_15 (.Di(reg8bit_8_out1), .en(decoder_5to32_2_uo[7]), .Do(BusA));
  Tri_state_Gate tri_state_gate_16 (.Di(reg8bit_8_out1), .en(decoder_5to32_3_uo[7]), .Do(BusB));
endmodule

module parity_check (
  input  [7:0] I,
  output O
);

  wire xor_1_out, xor_2_out, xor_3_out, xor_4_out, xor_5_out, xor_6_out;

  xor xor_1 (xor_1_out, I[0], I[1]);
  xor xor_2 (xor_2_out, I[2], I[3]);
  xor xor_3 (xor_3_out, I[4], I[5]);
  xor xor_4 (xor_4_out, I[6], I[7]);
  xor xor_5 (xor_5_out, xor_1_out, xor_2_out);
  xor xor_6 (xor_6_out, xor_3_out, xor_4_out);
  xor xor_7 (O, xor_5_out, xor_6_out);
endmodule

module ControlUnit (
  input  [7:0] OPcode,
  output [2:0] ALU_OP,
  output [2:0] beqN3,
  output PSW_W,
  output Brach,
  output MEMA1,
  output MEMA0,
  output MEMWD1,
  output MEMWD0,
  output MEW,
  output MER,
  output REG_WD2,
  output REG_WD1,
  output REG_WD0,
  output REGW,
  output jmp,
  output hlt
);

  wire and_3_out, and_4_out, and_5_out, and_6_out, and_8_out, and_9_out, and_12_out, and_13_out, and_15_out,
       and_16_out, nand_1_out, not_1_out, not_2_out, not_3_out, not_4_out, or_2_out, or_3_out, or_4_out,
       xor_1_out;
  wire [31:0] decoder_5to32_1_uo;

  decoder_5to32 decoder_5to32_1 (
    .a0(OPcode[3]), .a1(OPcode[4]), .a2(OPcode[5]), .a3(OPcode[6]), .a4(OPcode[7]),
    .uo({decoder_5to32_1_uo[31:19], hlt, decoder_5to32_1_uo[17:9], jmp, decoder_5to32_1_uo[7:0]}));
  not not_1 (not_1_out, decoder_5to32_1_uo[0]);
  not not_2 (not_2_out, OPcode[2]);
  not not_3 (not_3_out, OPcode[1]);
  not not_4 (not_4_out, OPcode[0]);
  nand nand_1 (nand_1_out, OPcode[1], OPcode[0]);
  xor xor_1 (xor_1_out, OPcode[2], OPcode[1]);
  and and_1 (MEMA1, nand_1_out, OPcode[2], decoder_5to32_1_uo[1], not_1_out);
  and and_2 (MEMA0, xor_1_out, not_4_out, not_1_out, decoder_5to32_1_uo[1]);
  and and_3 (and_3_out, not_1_out, decoder_5to32_1_uo[1], OPcode[2], not_3_out, OPcode[0]);
  or or_1 (MEMWD1, and_3_out, and_16_out);
  and and_4 (and_4_out, OPcode[1], OPcode[0]);
  and and_5 (and_5_out, OPcode[2], OPcode[0]);
  and and_6 (and_6_out, OPcode[2], OPcode[2]);
  or or_2 (or_2_out, and_4_out, and_5_out, and_6_out);
  and and_7 (MEMWD0, or_2_out, decoder_5to32_1_uo[1], not_1_out);
  and and_8 (and_8_out, not_2_out, OPcode[1], not_4_out);
  or or_3 (or_3_out, and_8_out, and_9_out);
  and and_9 (and_9_out, OPcode[2], not_3_out, not_4_out);
  and and_10 (MER, or_3_out, not_1_out, decoder_5to32_1_uo[1]);
  and and_11 (REG_WD0, not_1_out, decoder_5to32_1_uo[1], not_2_out, not_3_out);
  and and_12 (and_12_out, not_2_out, not_4_out);
  and and_13 (and_13_out, not_2_out, not_3_out);
  or or_4 (or_4_out, and_13_out, and_12_out, and_15_out);
  and and_14 (REGW, or_4_out, not_1_out, decoder_5to32_1_uo[1]);
  and and_15 (and_15_out, not_3_out, not_4_out);
  encoder_8to3 encoder_8to3_1 (
    .i0(decoder_5to32_1_uo[9]), .i1(decoder_5to32_1_uo[10]), .i2(decoder_5to32_1_uo[11]),
    .i3(decoder_5to32_1_uo[12]), .i4(decoder_5to32_1_uo[13]), .i5(decoder_5to32_1_uo[14]),
    .i6(decoder_5to32_1_uo[15]), .i7(decoder_5to32_1_uo[16]), .o2(beqN3[2]), .o1(beqN3[1]), .o0(beqN3[0]));
  and and_16 (and_16_out, not_1_out, decoder_5to32_1_uo[1], not_2_out, OPcode[1], OPcode[0]);
  and and_17 (REG_WD1, not_1_out, decoder_5to32_1_uo[1], not_2_out, not_3_out, OPcode[0]);
  or or_5 (Brach, decoder_5to32_1_uo[16], decoder_5to32_1_uo[9], decoder_5to32_1_uo[10], decoder_5to32_1_uo[11], decoder_5to32_1_uo[12], decoder_5to32_1_uo[13], decoder_5to32_1_uo[14], decoder_5to32_1_uo[15]);
  encoder_8to3 encoder_8to3_2 (
    .i0(decoder_5to32_1_uo[2]), .i1(decoder_5to32_1_uo[3]), .i2(decoder_5to32_1_uo[4]),
    .i3(decoder_5to32_1_uo[5]), .i4(decoder_5to32_1_uo[6]), .i5(decoder_5to32_1_uo[7]), .i6(1'b0), .i7(1'b0),
    .o2(ALU_OP[2]), .o1(ALU_OP[1]), .o0(ALU_OP[0]));
  or or_6 (PSW_W, decoder_5to32_1_uo[2], decoder_5to32_1_uo[3], decoder_5to32_1_uo[4], decoder_5to32_1_uo[5], decoder_5to32_1_uo[6], decoder_5to32_1_uo[7]);

  assign MEW = MEMWD0;
  assign REG_WD2 = MER;

  // Notes on the sheet:
  //   第一位保留
endmodule

module encoder_8to3 (
  input  i0,
  input  i1,
  input  i2,
  input  i3,
  input  i4,
  input  i5,
  input  i6,
  input  i7,
  output o2,
  output o1,
  output o0
);

  wire and_1_out, and_2_out, and_3_out, and_4_out, and_5_out, and_6_out, and_7_out, not_1_out, not_2_out,
       not_3_out, not_4_out, not_5_out, not_6_out, not_7_out;

  not not_1 (not_1_out, i0);
  not not_2 (not_2_out, i1);
  not not_3 (not_3_out, i2);
  not not_4 (not_4_out, i3);
  not not_5 (not_5_out, i4);
  not not_6 (not_6_out, i5);
  not not_7 (not_7_out, i6);
  // NOT_Gate not_8 has open pins: in=i7, out=open
  and and_1 (and_1_out, i1, not_1_out);
  and and_2 (and_2_out, not_1_out, not_2_out, i2);
  and and_3 (and_3_out, not_1_out, not_2_out, not_3_out, i3);
  and and_4 (and_4_out, not_1_out, not_2_out, i4, not_3_out, not_4_out);
  and and_5 (and_5_out, not_1_out, not_2_out, not_3_out, not_4_out, not_5_out, i5);
  and and_6 (and_6_out, not_1_out, not_2_out, not_3_out, not_6_out, not_4_out, not_5_out, i6);
  and and_7 (and_7_out, not_7_out, not_1_out, not_2_out, not_3_out, not_4_out, not_5_out, not_6_out, i7);
  or or_1 (o2, and_4_out, and_7_out, and_6_out, and_5_out);
  or or_2 (o1, and_2_out, and_6_out, and_7_out, and_3_out);
  or or_3 (o0, and_3_out, and_5_out, and_7_out, and_1_out);
endmodule

module brance_true_unit (
  input  [2:0] BEQ_code,
  input  [7:0] REG_PSW,
  output jmp
);

  wire and_1_out, and_2_out, and_3_out, and_4_out, and_5_out, and_6_out, and_7_out, and_8_out,
       decoder_3to8_1_y0, decoder_3to8_1_y1, decoder_3to8_1_y2, decoder_3to8_1_y3, decoder_3to8_1_y4,
       decoder_3to8_1_y5, decoder_3to8_1_y6, decoder_3to8_1_y7, not_1_out, not_2_out, not_3_out, not_4_out;

  decoder_3to8 decoder_3to8_1 (
    .a2(BEQ_code[2]), .a1(BEQ_code[1]), .a0(BEQ_code[0]), .y0(decoder_3to8_1_y0), .y1(decoder_3to8_1_y1),
    .y2(decoder_3to8_1_y2), .y3(decoder_3to8_1_y3), .y4(decoder_3to8_1_y4), .y5(decoder_3to8_1_y5),
    .y6(decoder_3to8_1_y6), .y7(decoder_3to8_1_y7));
  not not_1 (not_1_out, REG_PSW[0]);
  not not_2 (not_2_out, REG_PSW[1]);
  not not_3 (not_3_out, REG_PSW[2]);
  not not_4 (not_4_out, REG_PSW[3]);
  and and_1 (and_1_out, REG_PSW[1], decoder_3to8_1_y0);
  and and_2 (and_2_out, not_2_out, decoder_3to8_1_y1);
  and and_3 (and_3_out, REG_PSW[2], decoder_3to8_1_y2);
  and and_4 (and_4_out, not_3_out, decoder_3to8_1_y3);
  or or_1 (jmp, and_1_out, and_2_out, and_3_out, and_4_out, and_5_out, and_6_out, and_7_out, and_8_out);
  and and_5 (and_5_out, REG_PSW[3], decoder_3to8_1_y4);
  and and_6 (and_6_out, not_4_out, decoder_3to8_1_y5);
  and and_7 (and_7_out, REG_PSW[0], decoder_3to8_1_y6);
  and and_8 (and_8_out, not_1_out, decoder_3to8_1_y7);
endmodule

module selector_4 (
  input  a1,
  input  a0,
  input  [7:0] REG0,
  input  [7:0] REG1,
  input  [7:0] REG2,
  input  [7:0] REG3,
  output [7:0] WD
);

  wire decoder_2to4_1_y0, decoder_2to4_1_y1, decoder_2to4_1_y2, decoder_2to4_1_y3;

  decoder_2to4 decoder_2to4_1 (
    .a1(a1), .a0(a0), .y0(decoder_2to4_1_y0), .y1(decoder_2to4_1_y1), .y2(decoder_2to4_1_y2),
    .y3(decoder_2to4_1_y3));
  Tri_state_Gate tri_state_gate_1 (.Di(REG0), .en(decoder_2to4_1_y0), .Do(WD));
  Tri_state_Gate tri_state_gate_2 (.Di(REG1), .en(decoder_2to4_1_y1), .Do(WD));
  Tri_state_Gate tri_state_gate_3 (.Di(REG2), .en(decoder_2to4_1_y2), .Do(WD));
  Tri_state_Gate tri_state_gate_4 (.Di(REG3), .en(decoder_2to4_1_y3), .Do(WD));
endmodule

module selector_5 (
  input  a2,
  input  a1,
  input  a0,
  input  [7:0] REG0,
  input  [7:0] REG1,
  input  [7:0] REG2,
  input  [7:0] REG3,
  input  [7:0] REG4,
  output [7:0] WD
);

  wire decoder_2to4_1_y0, decoder_2to4_1_y1, decoder_2to4_1_y2, decoder_2to4_1_y3;
  wire [7:0] tri_state_gate_1_do;

  decoder_2to4 decoder_2to4_1 (
    .a1(a1), .a0(a0), .y0(decoder_2to4_1_y0), .y1(decoder_2to4_1_y1), .y2(decoder_2to4_1_y2),
    .y3(decoder_2to4_1_y3));
  Tri_state_Gate tri_state_gate_1 (.Di(REG0), .en(decoder_2to4_1_y0), .Do(tri_state_gate_1_do));
  Tri_state_Gate tri_state_gate_2 (.Di(REG1), .en(decoder_2to4_1_y1), .Do(tri_state_gate_1_do));
  Tri_state_Gate tri_state_gate_3 (.Di(REG2), .en(decoder_2to4_1_y2), .Do(tri_state_gate_1_do));
  Tri_state_Gate tri_state_gate_4 (.Di(REG3), .en(decoder_2to4_1_y3), .Do(tri_state_gate_1_do));
  decoder_1to2 decoder_1to2_1 (.i1(a2), .b(REG4), .a(tri_state_gate_1_do), .Do(WD));
endmodule

module BypassUnit (
  input  [7:0] ThisSRC,
  input  [7:0] ThisDES,
  input  [2:0] ThisADR,
  input  [7:0] LastDES,
  input  [2:0] LADR,
  input  LPSW_W,
  input  [7:0] LLastDES,
  input  [2:0] LLADR,
  input  LLPSW_W,
  input  PSW_W,
  output LLSRC,
  output LSRC,
  output LLDES,
  output LDES,
  output LLOP1,
  output LLOP0,
  output LOP1,
  output LOP0,
  output PSW,
  output BP
);

  wire and_1_out, and_2_out, and_3_out, and_4_out, and_5_out, and_6_out, and_7_out, and_8_out, and_9_out,
       and_10_out, and_11_out, and_12_out, and_13_out, data_comparator_1_o, data_comparator_3_o, not_1_out,
       not_4_out, not_6_out, not_7_out, not_8_out, or_1_out, or_2_out, or_3_out, or_4_out;
  wire [2:0] not_2_out, not_3_out, not_5_out;
  wire [7:0] decoder_1to2_1_do, decoder_1to2_2_do;

  not not_1 (not_1_out, PSW_W);
  assign not_2_out = ~ThisADR;  // NOT_Gate not_2, 3 bits wide
  assign not_3_out = ~LADR;  // NOT_Gate not_3, 3 bits wide
  and and_1 (and_1_out, not_1_out, not_2_out[2], not_2_out[1], ThisADR[0]);
  not not_4 (not_4_out, LLPSW_W);
  assign not_5_out = ~LLADR;  // NOT_Gate not_5, 3 bits wide
  decoder_1to2 decoder_1to2_1 (.i1(LLPSW_W), .b(8'h7), .a(LLastDES), .Do(decoder_1to2_1_do));
  decoder_1to2 decoder_1to2_2 (.i1(LPSW_W), .b(8'h7), .a(LastDES), .Do(decoder_1to2_2_do));
  and and_2 (and_2_out, not_1_out, not_2_out[2], ThisADR[1], ThisADR[0]);
  and and_3 (and_3_out, not_1_out, ThisADR[2], not_2_out[1], ThisADR[0]);
  not not_6 (not_6_out, LPSW_W);
  and and_4 (and_4_out, not_6_out, not_3_out[2], not_3_out[1], not_3_out[0]);
  and and_5 (and_5_out, not_4_out, not_5_out[2], not_5_out[1], not_5_out[0]);
  and and_6 (and_6_out, not_1_out, ThisADR[2], not_2_out[1], not_2_out[0]);
  and and_7 (and_7_out, not_6_out, not_3_out[2], not_3_out[1], LADR[0]);
  and and_8 (and_8_out, not_4_out, not_5_out[2], not_5_out[1], LLADR[0]);
  data_comparator data_comparator_1 (.a0(decoder_1to2_1_do), .a1(ThisSRC), .o(data_comparator_1_o));
  data_comparator data_comparator_2 (.a0(decoder_1to2_2_do), .a1(ThisSRC), .o(LSRC));
  data_comparator data_comparator_3 (.a0(LLastDES), .a1(ThisDES), .o(data_comparator_3_o));
  data_comparator data_comparator_4 (.a0(LastDES), .a1(ThisDES), .o(LDES));
  selector_BU selector_bu_1 (.PSW_W(LLPSW_W), .ADR(LLADR), .OP1(LLOP1), .OP0(LLOP0));
  selector_BU selector_bu_2 (.PSW_W(LPSW_W), .ADR(LADR), .OP1(LOP1), .OP0(LOP0));
  and and_9 (and_9_out, not_1_out, ThisADR[2], ThisADR[1], not_2_out[0]);
  and and_10 (and_10_out, not_6_out, LADR[2], not_3_out[1], not_3_out[0]);
  or or_1 (or_1_out, and_4_out, and_7_out, and_10_out, and_13_out, LPSW_W);
  and and_11 (and_11_out, not_4_out, LLADR[2], not_5_out[1], not_5_out[0]);
  and and_12 (and_12_out, not_4_out, LLADR[2], LLADR[1], not_5_out[0]);
  or or_2 (or_2_out, and_5_out, and_8_out, and_11_out, and_12_out, LLPSW_W);
  not not_7 (not_7_out, LSRC);
  not not_8 (not_8_out, LDES);
  or or_3 (or_3_out, and_1_out, and_2_out, and_3_out, and_6_out, and_9_out, PSW_W);
  and and_13 (and_13_out, not_6_out, LADR[2], LADR[1], not_3_out[0]);
  and and_14 (LLSRC, data_comparator_1_o, not_7_out);
  and and_15 (LLDES, data_comparator_3_o, not_8_out);
  or or_4 (or_4_out, or_1_out, or_2_out);
  and and_16 (BP, or_3_out, or_4_out);

  assign PSW = PSW_W;
endmodule

module data_comparator (
  input  [7:0] a0,
  input  [7:0] a1,
  output o
);

  wire [7:0] xnor_1_out;

  assign xnor_1_out = ~(a0 ^ a1);  // XNOR_Gate xnor_1, 8 bits wide
  and and_1 (o, xnor_1_out[0], xnor_1_out[1], xnor_1_out[2], xnor_1_out[3], xnor_1_out[4], xnor_1_out[5], xnor_1_out[6], xnor_1_out[7]);
endmodule

module selector_BU (
  input  PSW_W,
  input  [2:0] ADR,
  output OP1,
  output OP0
);

  wire and_1_out, and_2_out, and_3_out, not_1_out, not_2_out, not_3_out, not_4_out;

  not not_1 (not_1_out, PSW_W);
  not not_2 (not_2_out, ADR[0]);
  not not_3 (not_3_out, ADR[1]);
  not not_4 (not_4_out, ADR[2]);
  and and_1 (and_1_out, not_1_out, not_4_out, ADR[1], not_2_out);
  and and_2 (and_2_out, not_1_out, ADR[2], not_3_out, not_2_out);
  or or_1 (OP1, and_1_out, PSW_W, and_2_out);
  and and_3 (and_3_out, not_1_out, not_4_out, not_3_out, not_2_out);
  or or_2 (OP0, and_3_out, PSW_W);
endmodule

module selector_address1to2 (
  input  i1,
  input  [7:0] a,
  output [7:0] D1,
  output [7:0] Do
);

  wire not_1_out;

  not not_1 (not_1_out, i1);
  Tri_state_Gate tri_state_gate_1 (.Di(a), .en(not_1_out), .Do(Do));
  Tri_state_Gate tri_state_gate_2 (.Di(a), .en(i1), .Do(D1));
endmodule
